# Fritzing sketch smart-ball-balancer (saved by Fritzing 0.9.4)
breadboards: 1

parts:
  LED1 = LED - 5mm [color="Yellow (585nm)" package="5 mm [THT]"]
  LED2 = LED - 5mm [color="Green (565nm)" package="5 mm [THT]"]
  LED3 = LED - 5mm [color="Red (633nm)" package="5 mm [THT]"]
  LED4 = LED - 5mm [color="Red (633nm)" package="5 mm [THT]"]
  LED5 = LED - 5mm [color="Green (565nm)" package="5 mm [THT]"]
  LED6 = LED - 5mm [color="Yellow (585nm)" package="5 mm [THT]"]
  R1 = Resistor [tolerance=±5% resistance=220 package=THT]
  R2 = Resistor [tolerance=±5% resistance=220 package=THT]
  R3 = Resistor [tolerance=±5% resistance=220 package=THT]
  R4 = Resistor [tolerance=±5% resistance=220 package=THT]
  R5 = Resistor [tolerance=±5% resistance=220 package=THT]
  R6 = Resistor [tolerance=±5% resistance=220 package=THT]
  Part1 = Arduino Uno (Rev3)
  part = Basic Servo [part_number="X Servo"]
  Y_Servo = Basic Servo
  part_2 = Adafruit STMPE610 Breakout

nets:
  N1: LED1.cathode, R6.Pin_0
  Y-Y: LED1.anode, R5.Pin_1, Part1.D13/SCK
  N2: LED2.cathode, R5.Pin_0
  G-Y: LED2.anode, R4.Pin_1, Part1.D12/MISO
  N3: LED3.cathode, R4.Pin_0
  R-Y: LED3.anode, Part1.D11_PWM/MOSI
  N4: LED4.cathode, R1.Pin_0
  R-X: LED4.anode, Part1.D8
  N5: LED5.cathode, R2.Pin_0
  G-X: LED5.anode, R1.Pin_1, Part1.D9_PWM
  N6: LED6.cathode, R3.Pin_0
  Y-X: LED6.anode, R2.Pin_1, Part1.D10_PWM/SS
  GND: R3.Pin_1, R6.Pin_1, Part1.GND, part.gnd, Y_Servo.gnd, part_2.GND, part_2.MODE
  N7: Part1.A5/SCL, part_2.SCL_5V
  N8: Part1.A4/SDA, part_2.SDA_5V
  N9: Part1.D5_PWM, part.pulse
  N10: Part1.D6_PWM, Y_Servo.pulse
  5V: Part1.5V, part.vcc, Y_Servo.vcc, part_2.+5V

notes:
  LED Truth Table
  Pins R G Y
  Red H L L
  Green - H L
  Yellow - - H
  X+ / X- & Y+ / Y- on STMPE610 to resistive touch overlay

custom parts:
  Adafruit STMPE610 Breakout: Getting touchy performance with your screen's touch screen? Resistive touch screens are incredibly popular as overlays to TFT and LCD displays. Only problem is they require a bunch of analog pins and you have to keep polling them since the overlays themselves are basically just big potentiometers. If your microcontroller doesn't have analog inputs, or maybe you want just a way more elegant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
