# Fritzing sketch pid_test (saved by Fritzing 0.9.4)
breadboards: 1

parts:
  R1 = Resistor [tolerance=±5% resistance=4.7k package=THT]
  R2 = Rotary Potentiometer (Small) [maximum_resistance=10kΩ package=THT]
  LED1 = LED - 5mm [color="Green (560nm)" package="5 mm [THT]"]
  part = Basic Servo
  R3 = Trimmer Potentiometer [maximum_resistance=10kΩ package=THT]
  Part1 = Arduino Mega 2560 (Rev3)
  R4 = Resistor [tolerance=±5% resistance=1k package=THT]

nets:
  5V: R1.Pin_0, part.vcc, Part1.5V
  N1: R1.Pin_1, R2.leg2
  N2: R2.leg1, R3.leg2
  N3: R2.wiper, Part1.A8
  GND: LED1.cathode, part.gnd, R3.leg1, R3.wiper
  N4: LED1.anode, R4.Pin_0
  N5: part.pulse, Part1.D8_PWM
  N6: Part1.D7_PWM, R4.Pin_1

notes:
  <<<<---- linkage---->>>>
